# Fritzing sketch TimerHidroponia (saved by Fritzing 0.9.3b)
breadboards: 1

parts:
  Componente1 = Arduino Pro Mini (5V)
  S1 = Momentary Switch [package=ksa_sealed_tac_switch]
  S2 = Momentary Switch [package=ksa_sealed_tac_switch]
  LED1 = LED - 3mm [color="Red (633nm)" package="3 mm [THT]"]
  R1 = Resistor [tolerance=±5% resistance=220 package="0402 [SMD]"]
  R2 = Resistor [tolerance=±5% resistance=10k package="0603 [SMD]"]
  R3 = Resistor [tolerance=±5% resistance=10k package="0603 [SMD]"]
  ZS-042_RTC1 = ZS-042 RTC Module
  Grove1 = Grove OLED 128x96
  U5 = G3VM-61E1 [package=g3vm-61e1]

nets:
  N1: Componente1.A4, ZS-042_RTC1.SDA, Grove1.SDA
  N2: Componente1.A5, ZS-042_RTC1.SCL, Grove1.SCL
  GND: Componente1.GND, R1.Pin_0, R2.Pin_0, R3.Pin_0, ZS-042_RTC1.GND, Grove1.GND, U5.P$2
  VCC: Componente1.VCC, S1.4, S2.2, ZS-042_RTC1.VCC, Grove1.VCC, U5.P$1
  N3: Componente1.D5, LED1.cathode
  N4: Componente1.D4, S1.1, R2.Pin_1
  N5: Componente1.D3, U5.P$3
  N6: Componente1.D2, S2.3, R3.Pin_1
  N7: LED1.anode, R1.Pin_1

notes:
  Botão para acionamento manual da bomba d'água
  Botão para acionamento do LCD
  Rele para ligar e desligar a bomba d'água

// code stored in the sketch: TimerHidroponia.ino
#include <Wire.h>        //Biblioteca para manipulação do protocolo I2C
#include <DS3231.h>      //Biblioteca para manipulação do DS3231 https://github.com/jarzebski/Arduino-DS3231
#include <LiquidCrystal_I2C.h>
 
DS3231 rtc;              //Criação do objeto do tipo DS3231
RTCDateTime dataehora;   //Criação do objeto do tipo RTCDateTime
LiquidCrystal_I2C lcd(0x3F,2,1,0,4,5,6,7,3, POSITIVE);

int rele = 3;
int botao = 2;
int manual = 4; 
long tempoManual = 0;
int estaManual = 0; //0 - Não, 1 - Sim
int ledManual = 5;
int bomba = LOW;
 
void setup()
{
  Serial.begin(9600);
  pinMode(rele, OUTPUT);
  pinMode(botao, INPUT);
  pinMode(manual, INPUT);
  pinMode(ledManual, OUTPUT);
  lcd.begin (16,2);
  rtc.begin();

  lcd.clear();
  lcd.setBacklight(LOW);
 
  //rtc.setDateTime(__DATE__, __TIME__); //habilitar somente para ajustar a hora, depois comentar e compilar de novo
}
 
void loop()
{  
  if (estaManual == 0 && digitalRead(manual) == HIGH && bomba == HIGH)
    ModoManual();
    
  if (digitalRead(botao) == HIGH)
    MostraInfo();
    
  dataehora = rtc.getDateTime();
  
  if ((dataehora.minute >= 0 && dataehora.minute <15) ||
      (dataehora.minute >= 30 && dataehora.minute <45) ||
      estaManual == 1)
    bomba = LOW; //Liga o rele
  else
    bomba = HIGH; //Desliga o rele
    
  digitalWrite(rele, bomba);

  if (estaManual == 1)
    digitalWrite(ledManual, HIGH);

  if (estaManual == 1 && abs(TempoAgora() - tempoManual) > 60) {
    estaManual = 0;
    digitalWrite(ledManual, LOW);
  }
}

void MostraInfo() {
  lcd.setBacklight(HIGH);
  lcd.clear();
  PrintHoraTemp();
  PrintBomba();
  delay(10000);
  lcd.clear();
  lcd.setBacklight(LOW);
}

void PrintHoraTemp() {
  lcd.setCursor(0,0);
  if (dataehora.hour < 10)
    lcd.print("0");
    
  lcd.print(dataehora.hour);
  lcd.print(":");

  if (dataehora.minute < 10)
    lcd.print("0");
    
  lcd.print(dataehora.minute);
  lcd.print(" - "); 
  lcd.print(rtc.readTemperature());
}

void PrintBomba() {
  lcd.setCursor(0,1);
  lcd.print("Bomba: ");

  if (bomba == LOW)
    lcd.print("ON ");
  else
    lcd.print("OFF");
}

void ModoManual() {
  estaManual = 1;
  tempoManual = TempoAgora();
}

int TempoAgora() {
  return dataehora.second + dataehora.minute * 60 + dataehora.hour * 3600;
}
